# Fritzing sketch solar_heat_controller (saved by Fritzing 0.9.3b)
breadboards: 1

parts:
  U1 = ESP8266 WiFi Module [part_number=ESP8266]
  Part1 = Logic Level Converter
  LCM1602_IIC1 = generic_ic_dip_22_300mil.fzp [part_number="LCM1602 IIC" chip_label="LCM1602 IIC"]
  LCD1 = LCD screen
  J1 = Basic Servo
  R1 = Resistor [tolerance=±5% resistance=10k package=THT]
  R2 = Resistor [tolerance=±5% resistance=10k package=THT]
  R3 = Resistor [tolerance=±5% resistance=10k package=THT]
  Flash = Pushbutton [package="[THT]"]
  Reset = Pushbutton [package="[THT]"]
  DS2 = DS18B20 1-Wire Temperature Sensor [part_number=DS18B20]
  DS3 = DS18B20 1-Wire Temperature Sensor [part_number=DS18B20]
  1-wire_pull-up = Resistor [tolerance=±5% resistance=4.7k package=THT]
  DS4 = DS18B20 1-Wire Temperature Sensor [part_number=DS18B20]
  Q1 = Basic FET N-Channel [package="DPak [SMD]"]
  Fan = DC Motor

nets:
  N1: U1.IO0, Flash.Pin_1, Flash.Pin_2
  N2: U1.IO2, R1.Pin_0
  N3: U1.IO4, Part1.RX_LV
  N4: U1.3.3V#10, R1.Pin_1
  VDD: U1.3.3V#11, Part1.LV, R3.Pin_1, DS2.VDD, DS3.VDD, 1-wire_pull-up.Pin_1, DS4.VDD
  GND: U1.GND#12, Part1.GND, LCM1602_IIC1.connector16, J1.gnd, R2.Pin_1, Flash.Pin_3, Flash.Pin_4, Reset.Pin_2, DS2.GND, DS3.GND, DS4.GND, Q1.source
  N5: U1.IO5, J1.pulse
  N6: U1.RST, Reset.Pin_3, Reset.Pin_4
  N7: U1.CHIP_EN, R3.Pin_0
  N8: U1.IO14, DS2.DQ, DS3.DQ, 1-wire_pull-up.Pin_0, DS4.DQ
  N9: U1.IO12, Part1.TX2_LV
  N10: U1.IO13, Part1.RX2_LV
  N11: U1.IO15, R2.Pin_0
  N12: Part1.RX_HV, Q1.Gate
  N13: Part1.HV, LCM1602_IIC1.connector17, J1.vcc
  N14: Part1.RX2_HV, LCM1602_IIC1.connector19
  N15: Part1.TX2_HV, LCM1602_IIC1.connector18
  N16: LCM1602_IIC1.connector0, LCD1.VSS
  N17: LCM1602_IIC1.connector1, LCD1.VDD
  N18: LCM1602_IIC1.connector2, LCD1.V0
  N19: LCM1602_IIC1.connector3, LCD1.RS
  N20: LCM1602_IIC1.connector4, LCD1.R/W
  N21: LCM1602_IIC1.connector5, LCD1.E
  N22: LCM1602_IIC1.connector6, LCD1.DB0
  N23: LCM1602_IIC1.connector7, LCD1.DB1
  N24: LCM1602_IIC1.connector8, LCD1.DB2
  N25: LCM1602_IIC1.connector9, LCD1.DB3
  N26: LCM1602_IIC1.connector10, LCD1.DB4
  N27: LCM1602_IIC1.connector11, LCD1.DB5
  N28: LCM1602_IIC1.connector12, LCD1.DB6
  N29: LCM1602_IIC1.connector13, LCD1.DB7
  N30: LCM1602_IIC1.connector14, LCD1.LED+
  N31: LCM1602_IIC1.connector15, LCD1.LED-
  N32: Q1.drain, Fan.pin_1

notes:
  Solar cell. Voltage scaled to 0 - 1 volts.
  DC 12V
